# Fritzing sketch protoboard layout (saved by Fritzing 0.9.2b)

parts:
  Part2 = Logic Level Converter Bi-Directional BOB-12009
  U1 = ESP8266 WiFi Module [part_number=ESP8266]
  Part3 = Arduino Uno (Rev3)  # not connected
  R1 = Resistor [tolerance=±5% resistance=10k package="0603 [SMD]"]
  J1 = female alternating pin header, 6 pins [form="♀ (female)"]
  J4 = female alternating pin header, 6 pins [form="♀ (female)"]
  AM1 = AM2302 Humidity and Temperature Sensor
  J5 = female alternating pin header, 4 pins [form="♀ (female)"]
  J6 = female alternating pin header, 4 pins [form="♀ (female)"]
  J7 = female alternating pin header, 3 pins [form="♀ (female)"]
  Part1 = Arduino Prototyping Shield
  R2 = Resistor [tolerance=±5% resistance=10k package="0603 [SMD]"]
  IC1 = Voltage Regulator AMS1117 [package=sot223]
  C1 = Capacitor Polarized [package=cpol-radial-10uf-25v]
  R3 = Resistor [tolerance=±5% resistance=10k package="0603 [SMD]"]
  R4 = Resistor [tolerance=±5% resistance=10k package="0603 [SMD]"]
  R5 = Resistor [tolerance=±5% resistance=10k package="0603 [SMD]"]
  C2 = Capacitor Polarized [package=cpol-radial-100uf-25v]

nets:
  N1: Part2.LV4, U1.TXD, J4.pin6, J5.pin4, Part1.N$168, Part1.N$268
  N2: Part2.LV3, U1.RXD, J4.pin5, J6.pin1, Part1.N$108, Part1.N$240
  GND: Part2.GND, U1.GND, J1.pin4, J4.pin4, AM1.GND, J6.pin4, J7.pin3, Part1.GND, Part1.N$47, Part1.N$89, Part1.N$165, Part1.N$241, Part1.N$273, Part1.N$293, IC1.GND, C1.+, C2.+
  N3: Part2.LV, J4.pin3, Part1.N$107, Part1.N$201, Part1.N$238, Part1.N$242, Part1.N$272, Part1.N$415, Part1.N$416, R2.Pin_1, IC1.OUT, R3.Pin_1, R4.Pin_1, R5.Pin_1, C2.-
  N4: Part2.LV2, J4.pin2, Part1.N$418
  N5: Part2.LV1, J4.pin1, Part1.N$435
  N6: Part2.HV1, J1.pin1, Part1.N$430
  N7: Part2.HV2, J1.pin2, Part1.N$421
  VDD: Part2.HV, J1.pin3, AM1.VDD, J7.pin1, Part1.+5V, Part1.N$282, Part1.N$286, Part1.N$412, IC1.IN, C1.-
  N8: Part2.HV3, J1.pin5, Part1.D1(TX), Part1.N$309
  N9: Part2.HV4, J1.pin6, Part1.D0(RX), Part1.N$16
  N10: U1.VCC, J5.pin1, Part1.N$123, Part1.N$203, R5.Pin_0
  N11: U1.GPIO_0, J6.pin2, Part1.N$96, Part1.N$191, R4.Pin_0
  N12: U1.GPIO_16, J5.pin2, Part1.N$192
  N13: U1.GPIO_2, J6.pin3, Part1.N$91, Part1.N$179, R3.Pin_0
  N14: U1.CH_PD, J5.pin3, Part1.N$167, Part1.N$180, R2.Pin_0
  N15: R1.Pin_0, AM1.DATA, J7.pin2, Part1.N$46, Part1.N$410
  N16: R1.Pin_1, Part1.D2

notes:
  12/13 for Serial Output

custom parts:
  Logic Level Converter Bi-Directional BOB-12009: SparkFun product BOB-12009 If you’ve ever tried to connect a 3.3V device to a 5V system, you know what a challenge it can be. The SparkFun bi-directional logic level converter is a small device that safely steps down 5V signals to 3.3V AND steps up 3.3V to 5V at the same time. This level converter also works with 2.8V and 1.8V devices. What really separates this Logic level converter from our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
  ESP8266 WiFi Module: Generic WiFi Module based on the ESP8266 with onboard PCB antenna and UART communications
